# Fritzing sketch schematic (saved by Fritzing 0.9.3b)
breadboards: 1

parts:
  Part1 = Arduino Pro Mini (3.3V)
  NRF24L01 = NRF24L01
  V3 = DC Power [voltage=5]
  R1 = Resistor [tolerance=±5% resistance=1M package=THT]
  R2 = Resistor [tolerance=±5% resistance=470k package=THT]
  DHT22_humidity/temp = Humidity and Temperature Sensor RHT03
  Temperature_sensor = DS18B20 1-Wire Temperature Sensor [part_number=DS18B20]
  Ambient_light_sensor_BH1750FVI = VCNL4000 [package=vcnl4000]

nets:
  3.3V: Part1.VCC, NRF24L01.VCC, DHT22_humidity/temp.Vcc, Temperature_sensor.VDD, Ambient_light_sensor_BH1750FVI.VDD
  GND: Part1.GND, NRF24L01.GND, V3.V-, R2.Pin_1, DHT22_humidity/temp.GND_2, Temperature_sensor.GND, Ambient_light_sensor_BH1750FVI.GND
  N1: Part1.A4, Ambient_light_sensor_BH1750FVI.SDA
  N2: Part1.A5, Ambient_light_sensor_BH1750FVI.SCL
  4.5V: Part1.RAW, V3.V+, R1.Pin_0
  N3: Part1.A0, R1.Pin_1, R2.Pin_0
  N4: Part1.SCK, NRF24L01.SCK
  N5: Part1.MISO, NRF24L01.MISO
  N6: Part1.MOSI, NRF24L01.MOSI
  N7: Part1.D10, NRF24L01.CSN
  N8: Part1.D9, NRF24L01.CE
  N9: Part1.D7, DHT22_humidity/temp.Data-signal
  N10: Part1.D5, Temperature_sensor.DQ
  N11: Part1.D4, NRF24L01.IRQ
